# Fritzing sketch setup (saved by Fritzing 0.9.9b)
breadboards: 1

parts:
  WeMos_D1_R1 = WeMos D1 R2
  U1 = LCD-16X2 [package=lcd-16x2]
  R1 = Resistor [tolerance=±5% power=0.25 resistance=100 package=THT]
  R2 = Resistor [tolerance=±5% power=0.25 resistance=100 package=THT]
  LED1 = LED - 5mm [color="Red (633nm)" current=0.030 package="5 mm [THT]"]

nets:
  N1: WeMos_D1_R1.D2, U1.RS
  N2: WeMos_D1_R1.D3, U1.E
  N3: WeMos_D1_R1.D4, U1.DB4
  N4: WeMos_D1_R1.(D5), U1.DB5
  N5: WeMos_D1_R1.(D6), U1.DB6
  N6: WeMos_D1_R1.(D7), U1.DB7
  N7: WeMos_D1_R1.VIN, R1.Pin_0
  GND: WeMos_D1_R1.GND, U1.VSS, U1.VO, U1.R_W, U1.DB0, U1.DB1, U1.DB2, U1.DB3, U1.K, R2.Pin_1
  N8: U1.VDD, U1.A, R1.Pin_1
  N9: R2.Pin_0, LED1.cathode

custom parts:
  WeMos D1 R2: The D1 R2 is a mini wifi board based on the ESP-8266EX.
